// Logisim project cpu.circ as structural Verilog: 21 circuits, main circuit PC Count
module main (
  input  [15:0] From_Instr_Mem,
  input  clk,
  output [15:0] r0,
  output [15:0] r1,
  output [15:0] r2,
  output [15:0] r3,
  output [15:0] Display_0,
  output [15:0] Display_1,
  output [15:0] To_Instr_Mem,
  output [15:0] Data_Mem_Data,
  output [15:0] Data_Mem_Addr,
  output Data_Mem_Write
);

  wire ALU_signed_overflow, ALUeq, ALUSrc, Beq, BEQ_Eq, Bne, BNE_NEQ, BorJ, button_1_out, Display, JAL, Jump,
       MemToReg, not_1_out, not_2_out, RegWrite, SignExt;
  wire [1:0] multiplexer_2_out, RegDst, splitter_1_rd, splitter_1_rs, splitter_1_rt;
  wire [2:0] nPC_Sel;
  wire [3:0] alucontrol_1_realop, ALUOP, splitter_1_opcode;
  wire [5:0] splitter_1_funct;
  wire [7:0] splitter_1_imm;
  wire [11:0] jAddr;
  wire [15:0] adder_1_out, bit_extender_1_out, bit_extender_2_out, BranchOff, controlled_buffer_1_out,
       multiplexer_1_out, multiplexer_4_out, multiplexer_5_out, NextPC, nop_1_instrout, PC_1, rs, RWriteD;
  wire [31:16] register_1_q;

  // Probe on multiplexer_1_out
  Multiplexer #(.width(16)) multiplexer_1 (
    .in0(adder_1_out), .in1(NextPC), .out(multiplexer_1_out), .sel(BorJ));  // open: en
  Register #(.width(16)) PC (.D(multiplexer_1_out), .Q(To_Instr_Mem), .clk(clk));  // open: en, clr
  Adder #(.width(16)) adder_1 (.a(To_Instr_Mem), .b(16'h1), .out(adder_1_out));  // open: cin, cout
  PC_Count pc_count_1 (
    .PC(PC_1), .signExtImm(BranchOff), .BEQOK(BEQ_Eq), .BNEOK(BNE_NEQ), .jAddr(jAddr), .rs(rs),
    .npcSel(nPC_Sel), .nxtPC(NextPC));
  NOP nop_1 (
    .nPC_Sel(nPC_Sel), .Instr(From_Instr_Mem), .BEQOK(BEQ_Eq), .BNEOK(BNE_NEQ), .Jump(Jump),
    .InstrOut(nop_1_instrout));
  Register #(.width(32)) register_1 (
    .D({nop_1_instrout, adder_1_out}), .Q({register_1_q, PC_1}), .clk(clk));  // open: en, clr
  Splitter splitter_1 (
    .regIn(register_1_q), .funct(splitter_1_funct), .rd(splitter_1_rd), .rt(splitter_1_rt),
    .rs(splitter_1_rs), .opCode(splitter_1_opcode), .imm(splitter_1_imm), .addr(jAddr));
  assign bit_extender_1_out = {{8{1'b0}}, splitter_1_imm};  // Bit_Extender bit_extender_1
  assign bit_extender_2_out = {{8{splitter_1_imm[7]}}, splitter_1_imm};  // Bit_Extender bit_extender_2
  Control control_1 (
    .OpCode(splitter_1_opcode), .RegDst(RegDst), .MemToReg(MemToReg), .ALUOp(ALUOP),
    .MemWrite(Data_Mem_Write), .ALUSrc(ALUSrc), .SignExt(SignExt), .RegWrite(RegWrite), .nPC_Sel(nPC_Sel),
    .Display(Display), .jal(JAL), .Jump(Jump), .Beq(Beq), .Bne(Bne), .BorJ(BorJ));
  Multiplexer #(.select(2), .width(2)) multiplexer_2 (
    .in0(splitter_1_rt), .in1(splitter_1_rd), .in2(2'b11), .out(multiplexer_2_out), .sel(RegDst));  // open: in3, en
  Multiplexer #(.width(16)) multiplexer_3 (
    .in0(bit_extender_1_out), .in1(bit_extender_2_out), .out(BranchOff), .sel(SignExt));  // open: en
  // Probe on RWriteD
  // Probe on RWriteD
  AluControl alucontrol_1 (.AluOp(ALUOP), .funct(splitter_1_funct), .RealOp(alucontrol_1_realop));
  Regfile_main RegFile (
    .Read_register_1(splitter_1_rs), .Read_register_2(splitter_1_rt), .write_register(multiplexer_2_out),
    .write_data(RWriteD), .Reg_0_Value(r0), .Reg_1_Value(r1), .Reg_2_Value(r2), .Reg_3_Value(r3),
    .RegWrite(RegWrite), .clock(clk), .Read_Data_1(rs), .Read_Data_2(Data_Mem_Data));
  Hex_Digit_Display hex_digit_display_1 (.value(Display_0[15:12]));  // open: dp
  alu_main ALU (
    .switch__S(alucontrol_1_realop), .X(rs), .equal(ALUeq), .result(Data_Mem_Addr),
    .signed_overflow(ALU_signed_overflow), .Y(multiplexer_4_out));
  Multiplexer #(.width(16)) multiplexer_4 (
    .in0(Data_Mem_Data), .in1(BranchOff), .out(multiplexer_4_out), .sel(ALUSrc));  // open: en
  Hex_Digit_Display hex_digit_display_2 (.value(Display_0[11:8]));  // open: dp
  Hex_Digit_Display hex_digit_display_3 (.value(Display_0[7:4]));  // open: dp
  LED led_1 (.in(ALU_signed_overflow));
  not not_1 (not_1_out, ALUeq);
  Hex_Digit_Display hex_digit_display_4 (.value(Display_0[3:0]));  // open: dp
  disp disp_1 (.dispControl(Display), .clock(clk), .rs(rs), .imm(Data_Mem_Addr), .d0(Display_0), .d1(Display_1));
  and and_1 (BEQ_Eq, Beq, ALUeq);
  and and_2 (BNE_NEQ, Bne, not_1_out);
  Hex_Digit_Display hex_digit_display_5 (.value(Display_1[15:12]));  // open: dp
  Hex_Digit_Display hex_digit_display_6 (.value(Display_1[11:8]));  // open: dp
  assign controlled_buffer_1_out = Data_Mem_Write ? Data_Mem_Data : 16'bz;  // Controlled_Buffer controlled_buffer_1
  RAM #(.addrWidth(16), .dataWidth(16)) ram_1 (
    .addr(Data_Mem_Addr), .data(controlled_buffer_1_out), .sel(1'b1), .clk(clk), .ld(not_2_out),
    .clr(button_1_out));
  Button button_1 (.out(button_1_out));
  not not_2 (not_2_out, Data_Mem_Write);
  Hex_Digit_Display hex_digit_display_7 (.value(Display_1[7:4]));  // open: dp
  Hex_Digit_Display hex_digit_display_8 (.value(Display_1[3:0]));  // open: dp
  Multiplexer #(.width(16)) multiplexer_5 (
    .in0(Data_Mem_Addr), .in1(controlled_buffer_1_out), .out(multiplexer_5_out), .sel(MemToReg));  // open: en
  Multiplexer #(.width(16)) multiplexer_6 (.in0(multiplexer_5_out), .in1(PC_1), .out(RWriteD), .sel(JAL));  // open: en

  // Other names for the same wires on the sheet: ALUOut[15:0] = Data_Mem_Addr; d0[15:0] = Display_0;
  //   d1[15:0] = Display_1; DataIn[15:0] = Data_Mem_Data; MemWrite = Data_Mem_Write

  // Notes on the sheet:
  //   This is the current PC that you need to send as OUTPUT
  //   This is the instruction that you would receive as INPUT
  //   This is a CLK that is an INPUT driven from the harness.
  //   Remember, this circuit is loaded from the harness to be tested!
  //   DO NOT CHANGE THE LOCATIONS OF THE INPUTS/OUTPUTS! IF YOU DO SO, YOU NEED TO MAKE SURE THE PINS ARE AT THE RIGHT PLACE!
  //   These are OUTPUTS to the circuit
  //   Control
  //   ALUControl
  //   ALUSrc
  //   Disp
  //   These are OUTPUTS to the circuit
endmodule

module PC_Count (
  input  [15:0] PC,
  input  [15:0] signExtImm,
  input  BEQOK,
  input  BNEOK,
  input  [2:0] npcSel,
  input  [11:0] jAddr,
  input  [15:0] rs,
  output [15:0] nxtPC
);

  wire not_1_out;
  wire [15:0] adder_1_out, adder_2_out, adder_3_out, adder_4_out, and_1_out, and_2_out, bit_extender_1_out,
       bit_extender_2_out, multiplexer_1_out, multiplexer_2_out, or_1_out, or_2_out;

  Adder #(.width(16)) adder_1 (.a(PC), .b(signExtImm), .out(adder_1_out));  // open: cin, cout
  assign and_1_out = PC & 16'hf000;  // AND_Gate and_1, 16 bits wide
  assign and_2_out = PC & 16'hf000;  // AND_Gate and_2, 16 bits wide
  Adder #(.width(16)) adder_2 (.a(PC), .b(16'h1), .out(adder_2_out));  // open: cin, cout
  not not_1 (not_1_out, BEQOK);
  assign or_1_out = and_1_out | bit_extender_1_out;  // OR_Gate or_1, 16 bits wide
  assign bit_extender_1_out = {{4{1'b0}}, jAddr};  // Bit_Extender bit_extender_1
  assign or_2_out = and_2_out | bit_extender_2_out;  // OR_Gate or_2, 16 bits wide
  assign bit_extender_2_out = {{4{1'b0}}, jAddr};  // Bit_Extender bit_extender_2
  Adder #(.width(16)) adder_3 (.a(PC), .b(16'h1), .out(adder_3_out));  // open: cin, cout
  Adder #(.width(16)) adder_4 (.a(PC), .b(signExtImm), .out(adder_4_out));  // open: cin, cout
  Multiplexer #(.width(16)) multiplexer_1 (
    .in0(adder_2_out), .in1(adder_1_out), .out(multiplexer_1_out), .sel(not_1_out));  // open: en
  Multiplexer #(.width(16)) multiplexer_2 (
    .in0(adder_3_out), .in1(adder_4_out), .out(multiplexer_2_out), .sel(BEQOK));  // open: en
  Multiplexer #(.select(3), .width(16), .enable("false")) multiplexer_3 (
    .in0(PC), .in1(multiplexer_2_out), .in2(multiplexer_1_out), .in3(or_1_out), .in4(or_2_out), .in5(rs),
    .out(nxtPC), .sel(npcSel));  // open: in6, in7

  // Notes on the sheet:
  //   4 - J
  //   Legend
  //   0 - PC+1
  //   1 - BEQ
  //   2 - BNE
  //   3 - JAL
  //   5 - JR
endmodule

module Control (
  input  [3:0] OpCode,
  output [1:0] RegDst,
  output MemToReg,
  output [3:0] ALUOp,
  output MemWrite,
  output ALUSrc,
  output SignExt,
  output RegWrite,
  output [2:0] nPC_Sel,
  output Display,
  output jal,
  output Jump,
  output Beq,
  output Bne,
  output BorJ
);

  RegDst regdst_1 (.Inst(OpCode), .RegDest(RegDst));
  MemToReg memtoreg_1 (.Inst(OpCode), .MemToReg(MemToReg));
  MemWrite memwrite_1 (.Inst(OpCode), .MemWrite(MemWrite));
  AluSrc alusrc_1 (.Inst(OpCode), .AluSrc(ALUSrc));
  SignExt signext_1 (.Inst(OpCode), .SignExt(SignExt));
  RegWrite regwrite_1 (.Inst(OpCode), .RegWrite(RegWrite));
  nPC_Sel npc_sel_1 (.Inst(OpCode), .nPC_Sel(nPC_Sel));
  Display display_1 (.Inst(OpCode), .Display(Display));
  JAL jal_1 (.Inst(OpCode), .Branch(jal));
  Jump jump_1 (.Inst(OpCode), .Branch(Jump));
  Beq beq_1 (.Inst(OpCode), .Beq(Beq));
  Bne bne_1 (.Inst(OpCode), .Bne(Bne));
  BorJ borj_1 (.Inst(OpCode), .BorJ(BorJ));

  assign ALUOp = OpCode;

  // Notes on the sheet:
  //   Let ALU Control Handle
endmodule

module Splitter (
  input  [15:0] regIn,
  output [5:0] funct,
  output [1:0] rd,
  output [1:0] rt,
  output [1:0] rs,
  output [3:0] opCode,
  output [7:0] imm,
  output [11:0] addr
);


  assign addr = regIn[11:0];
  assign funct = regIn[5:0];
  assign imm = regIn[7:0];
  assign opCode = regIn[15:12];
  assign rd = regIn[7:6];
  assign rs = regIn[11:10];
  assign rt = regIn[9:8];
endmodule

module AluControl (
  input  [3:0] AluOp,
  input  [5:0] funct,
  output [3:0] RealOp
);

  wire comparator_1_eq;
  wire [3:0] adder_1_out, adder_2_out, adder_3_out, adder_4_out, RInst, subtractor_1_out, subtractor_2_out,
       subtractor_3_out, subtractor_4_out, subtractor_5_out, subtractor_6_out;

  // Probe on RInst
  Bit_Extender #(.in_width(6), .out_width(4)) bit_extender_1 (.in(funct), .out(RInst));
  Adder #(.width(4)) adder_1 (.a(AluOp), .b(4'b0111), .out(adder_1_out));  // open: cin, cout
  Adder #(.width(4)) adder_2 (.a(AluOp), .b(4'b0111), .out(adder_2_out));  // open: cin, cout
  Adder #(.width(4)) adder_3 (.a(AluOp), .b(4'b0111), .out(adder_3_out));  // open: cin, cout
  Adder #(.width(4)) adder_4 (.a(AluOp), .b(4'b0010), .out(adder_4_out));  // open: cin, cout
  Subtractor #(.width(4)) subtractor_1 (.a(AluOp), .b(4'b0101), .out(subtractor_1_out));  // open: bin, bout
  Subtractor #(.width(4)) subtractor_2 (.a(AluOp), .b(4'b0101), .out(subtractor_2_out));  // open: bin, bout
  Subtractor #(.width(4)) subtractor_3 (.a(AluOp), .b(4'b0110), .out(subtractor_3_out));  // open: bin, bout
  Subtractor #(.width(4)) subtractor_4 (.a(AluOp), .b(4'b0010), .out(subtractor_4_out));  // open: bin, bout
  Subtractor #(.width(4)) subtractor_5 (.a(AluOp), .b(4'b1000), .out(subtractor_5_out));  // open: bin, bout
  Subtractor #(.width(4)) subtractor_6 (.a(AluOp), .b(4'b0011), .out(subtractor_6_out));  // open: bin, bout
  Comparator #(.width(4)) comparator_1 (.a(4'b0000), .b(AluOp), .eq(comparator_1_eq));  // open: gt, lt
  Multiplexer #(.width(4)) multiplexer_1 (.in1(RInst), .out(RealOp), .sel(comparator_1_eq));  // open: in0, en
  Multiplexer #(.select(4), .width(4)) multiplexer_2 (
    .in1(adder_1_out), .in2(adder_2_out), .in3(adder_3_out), .in4(adder_4_out), .in5(subtractor_1_out),
    .in6(subtractor_2_out), .in7(4'b0000), .in8(4'b0000), .in9(4'b0000), .in10(4'b0000), .in11(4'b0000),
    .in12(subtractor_3_out), .in13(subtractor_4_out), .in14(subtractor_5_out), .in15(subtractor_6_out),
    .out(RealOp), .sel(AluOp));  // open: in0, en
endmodule

module disp (
  input  dispControl,
  input  clock,
  input  [15:0] rs,
  input  [15:0] imm,
  output [15:0] d0,
  output [15:0] d1
);

  wire and_1_out, and_2_out, comparator_1_eq, comparator_2_eq, imm_t;

  Bit_Extender #(.in_width(16), .out_width(1)) bit_extender_1 (.in(imm), .out(imm_t));
  Comparator #(.width(1)) comparator_1 (.a(imm_t), .b(1'b0), .eq(comparator_1_eq));  // open: gt, lt
  Comparator #(.width(1)) comparator_2 (.a(imm_t), .b(1'b1), .eq(comparator_2_eq));  // open: gt, lt
  and and_1 (and_1_out, dispControl, comparator_1_eq);
  and and_2 (and_2_out, dispControl, comparator_2_eq);
  Register #(.width(16)) register_1 (.D(rs), .en(and_1_out), .Q(d0), .clk(clock));  // open: clr
  Register #(.width(16)) register_2 (.D(rs), .en(and_2_out), .Q(d1), .clk(clock));  // open: clr

  // Other names for the same wires on the sheet: clk = clock; dispCtrl = dispControl
endmodule

module RegDst (
  input  [3:0] Inst,
  output [1:0] RegDest
);

  Multiplexer #(.select(4), .width(2)) multiplexer_1 (
    .in0(2'b01), .in1(2'b00), .in2(2'b00), .in3(2'b00), .in4(2'b00), .in5(2'b00), .in6(2'b00), .in7(2'b10),
    .in8(2'b00), .in9(2'b00), .in10(2'b00), .in11(2'b00), .in12(2'b00), .in13(2'b00), .in14(2'b00),
    .in15(2'b00), .out(RegDest), .sel(Inst));  // open: en

  // Other names for the same wires on the sheet: opCode[3:0] = Inst

  // Notes on the sheet:
  //   jal
  //   j
  //   jr
  //   beq
  //   bne
  //   sw
  //   disp
endmodule

module Beq (
  input  [3:0] Inst,
  output Beq
);

  Multiplexer #(.select(4)) multiplexer_1 (
    .in0(1'b0), .in1(1'b0), .in2(1'b0), .in3(1'b0), .in4(1'b0), .in5(1'b0), .in6(1'b0), .in7(1'b0),
    .in8(1'b0), .in9(1'b0), .in10(1'b1), .in11(1'b0), .in12(1'b0), .in13(1'b0), .in14(1'b0), .in15(1'b0),
    .out(Beq), .sel(Inst));  // open: en

  // Other names for the same wires on the sheet: opCode[3:0] = Inst

  // Notes on the sheet:
  //   jal
  //   j
  //   jr
  //   beq
  //   bne
  //   sw
  //   disp
endmodule

module MemRead (
  input  [3:0] Inst,
  output MemRead
);

  Multiplexer #(.select(4)) multiplexer_1 (
    .in0(1'b0), .in1(1'b0), .in2(1'b0), .in3(1'b0), .in4(1'b0), .in5(1'b0), .in6(1'b0), .in7(1'b0),
    .in8(1'b0), .in9(1'b0), .in10(1'b0), .in11(1'b0), .in12(1'b1), .in13(1'b0), .in14(1'b1), .in15(1'b0),
    .out(MemRead), .sel(Inst));  // open: en

  // Other names for the same wires on the sheet: opCode[3:0] = Inst

  // Notes on the sheet:
  //   jal
  //   j
  //   jr
  //   beq
  //   bne
  //   sw
  //   disp
endmodule

module MemToReg (
  input  [3:0] Inst,
  output MemToReg
);

  Multiplexer #(.select(4)) multiplexer_1 (
    .in0(1'b0), .in1(1'b0), .in2(1'b0), .in3(1'b0), .in4(1'b0), .in5(1'b0), .in6(1'b0), .in7(1'b0),
    .in8(1'b0), .in9(1'b0), .in10(1'b0), .in11(1'b0), .in12(1'b0), .in13(1'b0), .in14(1'b1), .in15(1'b0),
    .out(MemToReg), .sel(Inst));  // open: en

  // Other names for the same wires on the sheet: opCode[3:0] = Inst

  // Notes on the sheet:
  //   jal
  //   j
  //   jr
  //   beq
  //   bne
  //   sw
  //   disp
endmodule

module MemWrite (
  input  [3:0] Inst,
  output MemWrite
);

  Multiplexer #(.select(4)) multiplexer_1 (
    .in0(1'b0), .in1(1'b0), .in2(1'b0), .in3(1'b0), .in4(1'b0), .in5(1'b0), .in6(1'b0), .in7(1'b0),
    .in8(1'b0), .in9(1'b0), .in10(1'b0), .in11(1'b0), .in12(1'b1), .in13(1'b0), .in14(1'b0), .in15(1'b0),
    .out(MemWrite), .sel(Inst));  // open: en

  // Other names for the same wires on the sheet: opCode[3:0] = Inst

  // Notes on the sheet:
  //   jal
  //   j
  //   jr
  //   beq
  //   bne
  //   sw
  //   disp
endmodule

module AluSrc (
  input  [3:0] Inst,
  output AluSrc
);

  Multiplexer #(.select(4)) multiplexer_1 (
    .in0(1'b0), .in1(1'b1), .in2(1'b1), .in3(1'b1), .in4(1'b1), .in5(1'b1), .in6(1'b1), .in7(1'b0),
    .in8(1'b0), .in9(1'b0), .in10(1'b0), .in11(1'b0), .in12(1'b1), .in13(1'b1), .in14(1'b1), .in15(1'b1),
    .out(AluSrc), .sel(Inst));  // open: en

  // Other names for the same wires on the sheet: opCode[3:0] = Inst

  // Notes on the sheet:
  //   jal (j's dont matter)
  //   j
  //   jr
  //   beq
  //   bne
  //   sw
  //   disp
endmodule

module SignExt (
  input  [3:0] Inst,
  output SignExt
);

  Multiplexer #(.select(4)) multiplexer_1 (
    .in0(1'b0), .in1(1'b0), .in2(1'b0), .in3(1'b0), .in4(1'b1), .in5(1'b0), .in6(1'b0), .in7(1'b0),
    .in8(1'b0), .in9(1'b0), .in10(1'b1), .in11(1'b1), .in12(1'b1), .in13(1'b0), .in14(1'b1), .in15(1'b0),
    .out(SignExt), .sel(Inst));  // open: en

  // Other names for the same wires on the sheet: opCode[3:0] = Inst

  // Notes on the sheet:
  //   jal
  //   j
  //   jr
  //   beq
  //   bne
  //   sw
  //   disp
endmodule

module RegWrite (
  input  [3:0] Inst,
  output RegWrite
);

  Multiplexer #(.select(4)) multiplexer_1 (
    .in0(1'b1), .in1(1'b1), .in2(1'b1), .in3(1'b1), .in4(1'b1), .in5(1'b1), .in6(1'b1), .in7(1'b1),
    .in8(1'b0), .in9(1'b0), .in10(1'b0), .in11(1'b0), .in12(1'b0), .in13(1'b1), .in14(1'b1), .in15(1'b0),
    .out(RegWrite), .sel(Inst));  // open: en

  // Other names for the same wires on the sheet: opCode[3:0] = Inst

  // Notes on the sheet:
  //   jal
  //   j
  //   jr
  //   beq
  //   bne
  //   sw
  //   disp
endmodule

module nPC_Sel (
  input  [3:0] Inst,
  output [2:0] nPC_Sel
);

  Multiplexer #(.select(4), .width(3)) multiplexer_1 (
    .in0(3'b000), .in1(3'b000), .in2(3'b000), .in3(3'b000), .in4(3'b000), .in5(3'b000), .in6(3'b000),
    .in7(3'b011), .in8(3'b100), .in9(3'b101), .in10(3'b001), .in11(3'b010), .in12(3'b000), .in13(3'b000),
    .in14(3'b000), .in15(3'b000), .out(nPC_Sel), .sel(Inst));  // open: en

  // Other names for the same wires on the sheet: opCode[3:0] = Inst

  // Notes on the sheet:
  //   jal
  //   j
  //   jr
  //   beq
  //   bne
  //   sw
  //   disp
endmodule

module Display (
  input  [3:0] Inst,
  output Display
);

  Multiplexer #(.select(4)) multiplexer_1 (
    .in0(1'b0), .in1(1'b0), .in2(1'b0), .in3(1'b0), .in4(1'b0), .in5(1'b0), .in6(1'b0), .in7(1'b0),
    .in8(1'b0), .in9(1'b0), .in10(1'b0), .in11(1'b0), .in12(1'b0), .in13(1'b0), .in14(1'b0), .in15(1'b1),
    .out(Display), .sel(Inst));  // open: en

  // Other names for the same wires on the sheet: opCode[3:0] = Inst

  // Notes on the sheet:
  //   jal
  //   j
  //   jr
  //   beq
  //   bne
  //   sw
  //   disp
endmodule

module Jump (
  input  [3:0] Inst,
  output Branch
);

  Multiplexer #(.select(4)) multiplexer_1 (
    .in0(1'b0), .in1(1'b0), .in2(1'b0), .in3(1'b0), .in4(1'b0), .in5(1'b0), .in6(1'b0), .in7(1'b1),
    .in8(1'b1), .in9(1'b1), .in10(1'b0), .in11(1'b0), .in12(1'b0), .in13(1'b0), .in14(1'b0), .in15(1'b0),
    .out(Branch), .sel(Inst));  // open: en

  // Other names for the same wires on the sheet: opCode[3:0] = Inst

  // Notes on the sheet:
  //   jal
  //   j
  //   jr
  //   beq
  //   bne
  //   sw
  //   disp
endmodule

module JAL (
  input  [3:0] Inst,
  output Branch
);

  Multiplexer #(.select(4)) multiplexer_1 (
    .in0(1'b0), .in1(1'b0), .in2(1'b0), .in3(1'b0), .in4(1'b0), .in5(1'b0), .in6(1'b0), .in7(1'b1),
    .in8(1'b0), .in9(1'b0), .in10(1'b0), .in11(1'b0), .in12(1'b0), .in13(1'b0), .in14(1'b0), .in15(1'b0),
    .out(Branch), .sel(Inst));  // open: en

  // Other names for the same wires on the sheet: opCode[3:0] = Inst

  // Notes on the sheet:
  //   jal
  //   j
  //   jr
  //   beq
  //   bne
  //   sw
  //   disp
endmodule

module NOP (
  input  [2:0] nPC_Sel,
  input  [15:0] Instr,
  input  BEQOK,
  input  BNEOK,
  input  Jump,
  output [15:0] InstrOut
);

  wire and_1_out, and_2_out, comparator_1_eq, comparator_2_eq, or_1_out;

  Comparator #(.width(3)) comparator_1 (.a(nPC_Sel), .b(3'b001), .eq(comparator_1_eq));  // open: gt, lt
  Comparator #(.width(3)) comparator_2 (.a(nPC_Sel), .b(3'b010), .eq(comparator_2_eq));  // open: gt, lt
  and and_1 (and_1_out, comparator_1_eq, BEQOK);
  and and_2 (and_2_out, comparator_2_eq, BNEOK);
  Multiplexer #(.width(16)) multiplexer_1 (.in0(Instr), .in1({16{1'b0}}), .out(InstrOut), .sel(or_1_out));  // open: en
  or or_1 (or_1_out, and_1_out, and_2_out, Jump);
endmodule

module Bne (
  input  [3:0] Inst,
  output Bne
);

  Multiplexer #(.select(4)) multiplexer_1 (
    .in0(1'b0), .in1(1'b0), .in2(1'b0), .in3(1'b0), .in4(1'b0), .in5(1'b0), .in6(1'b0), .in7(1'b0),
    .in8(1'b0), .in9(1'b0), .in10(1'b0), .in11(1'b1), .in12(1'b0), .in13(1'b0), .in14(1'b0), .in15(1'b0),
    .out(Bne), .sel(Inst));  // open: en

  // Other names for the same wires on the sheet: opCode[3:0] = Inst

  // Notes on the sheet:
  //   jal
  //   j
  //   jr
  //   beq
  //   bne
  //   sw
  //   disp
endmodule

module BorJ (
  input  [3:0] Inst,
  output BorJ
);

  Multiplexer #(.select(4)) multiplexer_1 (
    .in0(1'b0), .in1(1'b0), .in2(1'b0), .in3(1'b0), .in4(1'b0), .in5(1'b0), .in6(1'b0), .in7(1'b1),
    .in8(1'b1), .in9(1'b1), .in10(1'b1), .in11(1'b1), .in12(1'b0), .in13(1'b0), .in14(1'b0), .in15(1'b0),
    .out(BorJ), .sel(Inst));  // open: en

  // Other names for the same wires on the sheet: opCode[3:0] = Inst

  // Notes on the sheet:
  //   jal
  //   j
  //   jr
  //   beq
  //   bne
  //   sw
  //   disp
endmodule
