// Logisim project Regfile.circ as structural Verilog: 1 circuit, main circuit main
module main (
  input  [1:0] Read_register_1,
  input  [1:0] Read_register_2,
  input  [1:0] write_register,
  input  [15:0] write_data,
  input  RegWrite,
  input  clock,
  output [15:0] Reg_0_Value,
  output [15:0] Reg_1_Value,
  output [15:0] Reg_2_Value,
  output [15:0] Reg_3_Value,
  output [15:0] Read_Data_1,
  output [15:0] Read_Data_2
);

  wire and_1_out, wrtsel0, wrtsel1, wrtsel2, wrtsel3;
  wire [15:0] inp0, inp1, inp2, inp3;

  and and_1 (and_1_out, 1'b1, RegWrite);
  Demultiplexer #(.select(2)) demultiplexer_1 (
    .out0(wrtsel0), .out1(wrtsel1), .out2(wrtsel2), .out3(wrtsel3), .in(and_1_out), .sel(write_register));  // open: en
  Multiplexer #(.width(16)) multiplexer_1 (.in0(Reg_0_Value), .in1(write_data), .out(inp0), .sel(wrtsel0));  // open: en
  Multiplexer #(.width(16)) multiplexer_2 (.in0(Reg_1_Value), .in1(write_data), .out(inp1), .sel(wrtsel1));  // open: en
  Multiplexer #(.width(16)) multiplexer_3 (.in0(Reg_2_Value), .in1(write_data), .out(inp2), .sel(wrtsel2));  // open: en
  Multiplexer #(.width(16)) multiplexer_4 (.in0(Reg_3_Value), .in1(write_data), .out(inp3), .sel(wrtsel3));  // open: en
  Register #(.width(16)) Reg0 (.D(inp0), .Q(Reg_0_Value), .clk(clock));  // open: en, clr
  Register #(.width(16)) Reg1 (.D(inp1), .Q(Reg_1_Value), .clk(clock));  // open: en, clr
  Register #(.width(16)) Reg2 (.D(inp2), .Q(Reg_2_Value), .clk(clock));  // open: en, clr
  Register #(.width(16)) Reg3 (.D(inp3), .Q(Reg_3_Value), .clk(clock));  // open: en, clr
  Multiplexer #(.select(2), .width(16)) multiplexer_5 (
    .in0(Reg_0_Value), .in1(Reg_1_Value), .in2(Reg_2_Value), .in3(Reg_3_Value), .out(Read_Data_1),
    .sel(Read_register_1));  // open: en
  Multiplexer #(.select(2), .width(16)) multiplexer_6 (
    .in0(Reg_0_Value), .in1(Reg_1_Value), .in2(Reg_2_Value), .in3(Reg_3_Value), .out(Read_Data_2),
    .sel(Read_register_2));  // open: en

  // Other names for the same wires on the sheet: clk = clock; dat1[15:0] = Read_Data_1; dat2[15:0] = Read_Data_2;
  //   out0[15:0] = Reg_0_Value; out1[15:0] = Reg_1_Value; out2[15:0] = Reg_2_Value; out3[15:0] = Reg_3_Value;
  //   sel1[1:0] = Read_register_1; sel2[1:0] = Read_register_2; test[15:0] = write_data; wrt = RegWrite;
  //   wrtsel[1:0] = write_register

  // Notes on the sheet:
  //   These are INPUTS to the circuit
  //   These are INPUTS to the circuit
  //   DO NOT CHANGE THE LOCATIONS OF THE INPUTS/OUTPUTS! IF YOU DO SO, YOU NEED TO MAKE SURE THE PINS ARE AT THE RIGHT PLACE!
  //   These are OUTPUTS to the circuit
  //   Yet again, the clock is not an actual clock, but an input, one that will should/will be inputed from the higher circuit
  //   These are OUTPUTS to the circuit
endmodule
