// Logisim project alu.circ as structural Verilog: 6 circuits, main circuit main
module main (
  input  [15:0] X,
  input  [15:0] Y,
  input  [3:0] switch__S,
  output signed_overflow,
  output [15:0] result,
  output equal
);

  wire comparator_1_lt;
  wire [3:0] shfty;
  wire [15:0] addR, and_1_out, bc_1_bcout, bit_extender_1_out, ffo_1_ffoout, lui_1_luiout, or_1_out,
       shifter_1_out, shifter_2_out, shifter_3_out, subR, zb_1_zbout;

  // Probe on X
  // Probe on Y
  Comparator #(.width(16)) comparator_1 (.a(X), .b(Y), .eq(equal), .lt(comparator_1_lt));  // open: gt
  Shifter #(.width(16)) shifter_1 (.in(X), .\dist (shfty), .out(shifter_1_out));
  Shifter #(.width(16), .shift("lr")) shifter_2 (.in(X), .\dist (shfty), .out(shifter_2_out));
  Shifter #(.width(16), .shift("ar")) shifter_3 (.in(X), .\dist (shfty), .out(shifter_3_out));
  Adder #(.width(16)) adder_1 (.a(X), .b(Y), .out(addR));  // open: cin, cout
  Subtractor #(.width(16)) subtractor_1 (.a(X), .b(Y), .out(subR));  // open: bin, bout
  ffo ffo_1 (.x(X), .ffoOut(ffo_1_ffoout));
  zb zb_1 (.x(X), .zbOut(zb_1_zbout));
  bc bc_1 (.x(X), .bcOut(bc_1_bcout));
  lui lui_1 (.x(Y), .luiOut(lui_1_luiout));
  assign and_1_out = X & Y;  // AND_Gate and_1, 16 bits wide
  assign or_1_out = X | Y;  // OR_Gate or_1, 16 bits wide
  // Probe on addR
  assign bit_extender_1_out = {{15{1'b0}}, comparator_1_lt};  // Bit_Extender bit_extender_1
  Multiplexer #(.select(4), .width(16)) multiplexer_1 (
    .in0(and_1_out), .in1(or_1_out), .in2(bit_extender_1_out), .in3(shifter_1_out), .in4(shifter_2_out),
    .in5(shifter_3_out), .in6(addR), .in7(subR), .in8(ffo_1_ffoout), .in9(zb_1_zbout), .in10(bc_1_bcout),
    .in11(lui_1_luiout), .in12(Y), .out(result), .sel(switch__S));  // open: in13, in14, in15, en
  // Probe on result
  BitSelector #(.width(16), .group(4)) bitselector_1 (.in(Y), .out(shfty), .sel(2'b00));
  overflow overflow_1 (.x(X), .y(Y), .addR(addR), .subR(subR), .rselect(switch__S), .overflow(signed_overflow));

  // Other names for the same wires on the sheet: oflow = signed_overflow; rsel[3:0] = switch__S; shft[15:0] = Y;
  //   tunnel = equal

  // Notes on the sheet:
  //   These are INPUTS to your circuit
  //   This is an INPUT to your circuit
  //   Legend
  //   0 - AND
  //   1 - OR
  //   2 - SLT
  //   3 - SLLV
  //   4 - SRLV
  //   5 - SRAV
  //   6 - ADD
  //   7 - SUB
  //   8 - FFO
  //   9 - ZB
  //   10 - BC
  //   11 - LUI
  //   12 - DISP
  //   Display
  //   DO NOT CHANGE THE LOCATIONS OF THE INPUTS/OUTPUTS! IF YOU DO SO, YOU NEED TO MAKE SURE THE PINS ARE AT THE RIGHT PLACE!
  //   These are OUTPUTS to your circuit
endmodule

module overflow (
  input  [15:0] x,
  input  [15:0] y,
  input  [15:0] addR,
  input  [15:0] subR,
  input  [3:0] rselect,
  output overflow
);

  wire and_1_out, and_2_out, and_3_out, and_4_out, and_5_out, and_6_out, Azero, comparator_5_eq,
       comparator_6_eq, negAddR, negSubR, negX, negY, or_1_out, or_2_out, or_3_out, or_4_out, or_5_out,
       posAddR, posSubR, posX, posY, Szero;

  Comparator #(.width(16)) comparator_1 (.a(x), .b({16{1'b0}}), .gt(posX), .lt(negX));  // open: eq
  Comparator #(.width(16)) comparator_2 (.a(y), .b({16{1'b0}}), .gt(posY), .lt(negY));  // open: eq
  Comparator #(.width(16)) comparator_3 (.a(addR), .b({16{1'b0}}), .gt(posAddR), .eq(Azero), .lt(negAddR));
  Comparator #(.width(16)) comparator_4 (.a(subR), .b({16{1'b0}}), .gt(posSubR), .eq(Szero), .lt(negSubR));
  or or_1 (or_1_out, posAddR, Azero);
  or or_2 (or_2_out, negSubR, Szero);
  or or_3 (or_3_out, posSubR, Szero);
  and and_1 (and_1_out, posX, posY, negAddR);
  and and_2 (and_2_out, negX, negY, or_1_out);
  and and_3 (and_3_out, posX, negY, or_2_out);
  or or_4 (or_4_out, and_3_out, and_4_out);
  and and_4 (and_4_out, negX, posY, or_3_out);
  Comparator #(.width(4)) comparator_5 (.a(rselect), .b(4'b0111), .eq(comparator_5_eq));  // open: gt, lt
  or or_5 (or_5_out, and_1_out, and_2_out);
  Comparator #(.width(4)) comparator_6 (.a(rselect), .b(4'b0110), .eq(comparator_6_eq));  // open: gt, lt
  and and_5 (and_5_out, or_4_out, comparator_5_eq);
  and and_6 (and_6_out, or_5_out, comparator_6_eq);
  or or_6 (overflow, and_5_out, and_6_out);

  // Other names for the same wires on the sheet: rsel[3:0] = rselect
endmodule

module ffo (
  input  [15:0] x,
  output [15:0] ffoOut
);

  wire bitfinder_1_found;
  wire [3:0] bitfinder_1_index;
  wire [15:0] adder_1_out, bit_extender_1_out, subtractor_1_out;

  // Probe on bitfinder_1_index
  BitFinder #(.width(16), .\type ("high1")) bitfinder_1 (.in(x), .index(bitfinder_1_index), .found(bitfinder_1_found));
  assign bit_extender_1_out = {{12{1'b0}}, bitfinder_1_index};  // Bit_Extender bit_extender_1
  // Probe on 16'h10
  Adder #(.width(16)) adder_1 (.a(16'h1), .b(bit_extender_1_out), .out(adder_1_out));  // open: cin, cout
  Subtractor #(.width(16)) subtractor_1 (.a(16'h10), .b(adder_1_out), .out(subtractor_1_out));  // open: bin, bout
  Multiplexer #(.width(16)) multiplexer_1 (
    .in0(16'h10), .in1(subtractor_1_out), .out(ffoOut), .sel(bitfinder_1_found));  // open: en
endmodule

module zb (
  input  [15:0] x,
  output [15:0] zbOut
);

  wire comparator_1_eq, comparator_2_eq, or_1_out;

  Comparator comparator_1 (.a({8{1'b0}}), .b(x[7:0]), .eq(comparator_1_eq));  // open: gt, lt
  Comparator comparator_2 (.a(x[15:8]), .b({8{1'b0}}), .eq(comparator_2_eq));  // open: gt, lt
  or or_1 (or_1_out, comparator_1_eq, comparator_2_eq);
  assign zbOut = {{15{1'b0}}, or_1_out};  // Bit_Extender bit_extender_1
endmodule

module bc (
  input  [15:0] x,
  output [15:0] bcOut
);

  wire [4:0] bitadder_1_out;

  BitAdder #(.width(16)) bitadder_1 (.in0(x), .out(bitadder_1_out));
  assign bcOut = {{11{1'b0}}, bitadder_1_out};  // Bit_Extender bit_extender_1
endmodule

module lui (
  input  [15:0] x,
  output [15:0] luiOut
);

  Shifter #(.width(16)) shifter_1 (.in(x), .\dist (4'b1000), .out(luiOut));
endmodule
